// Logisim project cpu.circ as structural Verilog: 8 circuits, main circuit main
module main (
  input  reset
);

  wire ALUinB, and_1_out, BEQ, BR, CLK, DMwe, inpu, JAL, JP, JR, keyboard_1_avail, memory_latch_1_oe_latched,
       memory_latch_1_we_latched, multiplexer_4_out, nor_1_out, nor_2_out, not_1_out, not_2_out, not_3_out,
       outpu, Rdst, Rwd, Rwe;
  wire [2:0] ALUop, multiplexer_2_out, Rd, ReadReg1, ReadReg2, Shamt, WriteReg;
  wire [5:0] Immediate;
  wire [6:0] bit_extender_3_out, keyboard_1_data;
  wire [11:0] Address;
  wire [15:0] bit_extender_1_out, bit_extender_2_out, bit_extender_4_out, Instruction, JALval,
       memory_latch_1_address_latched, memory_latch_1_data_in_latched, multiplexer_1_out, multiplexer_5_out,
       multiplexer_6_out, multiplexer_7_out, multiplexer_8_out, multiplexer_10_out, NextInstructionC,
       OutputData, ram_1_dout, ReadData1, registerfile_1_readdata2, ripplecarryadder_2_result,
       singleregister_1_q, WriteData;

  Clock clock_1 (.out(CLK));
  InstructionDecoder instructiondecoder_1 (
    .Instruction(Instruction), .Address(Address), .Immediate(Immediate), .Rs(ReadReg1), .Rt(ReadReg2),
    .Rd(Rd), .Shamt(Shamt), .Rwe(Rwe), .Rdst(Rdst), .ALUinB(ALUinB), .ALUop2(ALUop[2]), .ALUop1(ALUop[1]),
    .ALUop0(ALUop[0]), .DMwe(DMwe), .Rwd(Rwd), .BR(BR), .JP(JP), .JR(JR), .BEQ(BEQ), .JAL(JAL), .inpu(inpu),
    .outpu(outpu));
  SingleRegister singleregister_1 (
    .CLK(not_1_out), .WE(1'b1), .Q(singleregister_1_q), .reset(reset), .D(NextInstructionC));
  not not_1 (not_1_out, CLK);
  RegisterFile registerfile_1 (
    .Reset(reset), .ReadReg1(ReadReg1), .ReadReg2(ReadReg2), .WriteReg(WriteReg), .CLK(CLK),
    .RegWriteEnable(Rwe), .WriteData(WriteData), .ReadData1(ReadData1), .ReadData2(registerfile_1_readdata2));
  ROM #(.addrWidth(16), .dataWidth(16)) rom_1 (.addr(singleregister_1_q), .data(Instruction));
  Multiplexer #(.width(16), .enable("false")) multiplexer_1 (
    .in0(registerfile_1_readdata2), .in1(bit_extender_1_out), .out(multiplexer_1_out), .sel(ALUinB));
  assign bit_extender_1_out = {{10{Immediate[5]}}, Immediate};  // Bit_Extender bit_extender_1
  Multiplexer #(.width(3), .enable("false")) multiplexer_2 (
    .in0(ReadReg2), .in1(Rd), .out(multiplexer_2_out), .sel(Rdst));
  Multiplexer #(.width(3), .enable("false")) multiplexer_3 (
    .in0(multiplexer_2_out), .in1(3'b111), .out(WriteReg), .sel(JAL));
  RippleCarryAdder ripplecarryadder_1 (.A(singleregister_1_q), .sub(1'b0), .B(16'h1), .result(JALval));  // open: ovf
  ALU alu_1 (
    .OpType(ALUop), .InputData1(ReadData1), .InputData2(multiplexer_1_out), .Shamt(Shamt),
    .OutputData(OutputData));
  assign bit_extender_2_out = {{10{Immediate[5]}}, Immediate};  // Bit_Extender bit_extender_2
  not not_2 (not_2_out, CLK);
  RAM #(.addrWidth(16), .dataWidth(16), .trigger("high"), .databus("bibus")) ram_1 (
    .addr(memory_latch_1_address_latched), .we(memory_latch_1_we_latched), .oe(memory_latch_1_oe_latched),
    .din(memory_latch_1_data_in_latched), .dout(ram_1_dout));
  memory_latch memory_latch_1 (
    .OE_latched(memory_latch_1_oe_latched), .WE_latched(memory_latch_1_we_latched),
    .address_latched(memory_latch_1_address_latched), .data_in(registerfile_1_readdata2), .clk(not_2_out),
    .WE(DMwe), .address(OutputData), .data_in_latched(memory_latch_1_data_in_latched));
  nor nor_1 (nor_1_out, OutputData[15], nor_2_out);
  nor nor_2 (nor_2_out, OutputData[0], OutputData[1], OutputData[2], OutputData[3], OutputData[4], OutputData[5], OutputData[6], OutputData[7], OutputData[8], OutputData[9], OutputData[10], OutputData[11], OutputData[12], OutputData[13], OutputData[14], OutputData[15]);
  RippleCarryAdder ripplecarryadder_2 (
    .A(JALval), .sub(1'b0), .B(bit_extender_2_out), .result(ripplecarryadder_2_result));  // open: ovf
  Multiplexer #(.enable("false")) multiplexer_4 (.in0(nor_1_out), .in1(nor_2_out), .out(multiplexer_4_out), .sel(BEQ));
  Bit_Extender #(.in_width(16), .out_width(7), .\type ("zero")) bit_extender_3 (
    .in(ReadData1), .out(bit_extender_3_out));
  Multiplexer #(.width(16), .enable("false")) multiplexer_5 (
    .in0(JALval), .in1(ripplecarryadder_2_result), .out(multiplexer_5_out), .sel(and_1_out));
  and and_1 (and_1_out, BR, multiplexer_4_out);
  TTY #(.rows(13), .cols(80)) tty_1 (.data(bit_extender_3_out), .clk(CLK), .we(outpu), .clr(reset));
  assign bit_extender_4_out = {{4{1'b0}}, Address};  // Bit_Extender bit_extender_4
  Multiplexer #(.width(16), .enable("false")) multiplexer_6 (
    .in0(OutputData), .in1(ram_1_dout), .out(multiplexer_6_out), .sel(Rwd));
  Multiplexer #(.width(16), .enable("false")) multiplexer_7 (
    .in0(multiplexer_5_out), .in1(bit_extender_4_out), .out(multiplexer_7_out), .sel(JP));
  Multiplexer #(.width(16), .enable("false")) multiplexer_8 (
    .in0(multiplexer_6_out), .in1(JALval), .out(multiplexer_8_out), .sel(JAL));
  Keyboard keyboard_1 (.clk(not_3_out), .re(inpu), .clr(reset), .avail(keyboard_1_avail), .data(keyboard_1_data));
  not not_3 (not_3_out, CLK);
  Multiplexer #(.width(16), .enable("false")) multiplexer_9 (
    .in0(multiplexer_7_out), .in1(ReadData1), .out(NextInstructionC), .sel(JR));
  Multiplexer #(.width(16), .enable("false")) multiplexer_10 (
    .in0(16'h80), .in1({{9{1'b0}}, keyboard_1_data}), .out(multiplexer_10_out), .sel(keyboard_1_avail));
  Multiplexer #(.width(16), .enable("false")) multiplexer_11 (
    .in0(multiplexer_8_out), .in1(multiplexer_10_out), .out(WriteData), .sel(inpu));

  // Other names for the same wires on the sheet: Rs[2:0] = ReadReg1; Rt[2:0] = ReadReg2

  // Notes on the sheet:
  //   contents of rom_1 (hex, n*v repeats v):
  //   e040 c20d e240 c20d e240 c209 e240 8380 e044 2013 e040 c20d e240 c20d e240 c209 e241 7340 603f edbd
  //   7cc0 7d01 7dc2 e081 5281 4022 f058 e27f 2013 f160 e67e 2013 fb28 4023 e141 8cc0 8d01 8dc2 ed83 3e00
endmodule

module SingleRegister (
  input  [15:0] D,
  input  reset,
  input  WE,
  input  CLK,
  output [15:0] Q
);

  wire DWE;

  and and_1 (DWE, WE, CLK);
  D_Flip_Flop d_ff_1 (.D(D[0]), .clk(DWE), .Q(Q[0]), .reset(reset));  // open: Qn, preset
  D_Flip_Flop d_ff_2 (.D(D[1]), .clk(DWE), .Q(Q[1]), .reset(reset));  // open: Qn, preset
  D_Flip_Flop d_ff_3 (.D(D[2]), .clk(DWE), .Q(Q[2]), .reset(reset));  // open: Qn, preset
  D_Flip_Flop d_ff_4 (.D(D[3]), .clk(DWE), .Q(Q[3]), .reset(reset));  // open: Qn, preset
  D_Flip_Flop d_ff_5 (.D(D[4]), .clk(DWE), .Q(Q[4]), .reset(reset));  // open: Qn, preset
  D_Flip_Flop d_ff_6 (.D(D[5]), .clk(DWE), .Q(Q[5]), .reset(reset));  // open: Qn, preset
  D_Flip_Flop d_ff_7 (.D(D[6]), .clk(DWE), .Q(Q[6]), .reset(reset));  // open: Qn, preset
  D_Flip_Flop d_ff_8 (.D(D[7]), .clk(DWE), .Q(Q[7]), .reset(reset));  // open: Qn, preset
  D_Flip_Flop d_ff_9 (.D(D[8]), .clk(DWE), .Q(Q[8]), .reset(reset));  // open: Qn, preset
  D_Flip_Flop d_ff_10 (.D(D[9]), .clk(DWE), .Q(Q[9]), .reset(reset));  // open: Qn, preset
  D_Flip_Flop d_ff_11 (.D(D[10]), .clk(DWE), .Q(Q[10]), .reset(reset));  // open: Qn, preset
  D_Flip_Flop d_ff_12 (.D(D[11]), .clk(DWE), .Q(Q[11]), .reset(reset));  // open: Qn, preset
  D_Flip_Flop d_ff_13 (.D(D[12]), .clk(DWE), .Q(Q[12]), .reset(reset));  // open: Qn, preset
  D_Flip_Flop d_ff_14 (.D(D[13]), .clk(DWE), .Q(Q[13]), .reset(reset));  // open: Qn, preset
  D_Flip_Flop d_ff_15 (.D(D[14]), .clk(DWE), .Q(Q[14]), .reset(reset));  // open: Qn, preset
  D_Flip_Flop d_ff_16 (.D(D[15]), .clk(DWE), .Q(Q[15]), .reset(reset));  // open: Qn, preset
endmodule

module RegisterFile (
  input  Reset,
  input  [2:0] ReadReg1,
  input  [2:0] ReadReg2,
  input  [2:0] WriteReg,
  input  CLK,
  input  RegWriteEnable,
  input  [15:0] WriteData,
  output [15:0] ReadData1,
  output [15:0] ReadData2
);

  wire rd_0, rd_1, rd_2, rd_3, rd_4, rd_5, rd_6, rd_7, rs1_0, rs1_1, rs1_2, rs1_3, rs1_4, rs1_5, rs1_6,
       rs1_7, rs2_0, rs2_1, rs2_2, rs2_3, rs2_4, rs2_5, rs2_6, rs2_7, WE_0, WE_1, WE_2, WE_3, WE_4, WE_5,
       WE_6, WE_7;
  wire [15:0] singleregister_1_q, singleregister_2_q, singleregister_3_q, singleregister_4_q,
       singleregister_5_q, singleregister_6_q, singleregister_7_q, singleregister_8_q;

  SingleRegister singleregister_1 (.CLK(CLK), .WE(WE_0), .Q(singleregister_1_q), .reset(Reset), .D({16{1'b0}}));
  SingleRegister singleregister_2 (.CLK(CLK), .WE(WE_1), .Q(singleregister_2_q), .reset(Reset), .D(WriteData));
  SingleRegister singleregister_3 (.CLK(CLK), .WE(WE_2), .Q(singleregister_3_q), .reset(Reset), .D(WriteData));
  SingleRegister singleregister_4 (.CLK(CLK), .WE(WE_3), .Q(singleregister_4_q), .reset(Reset), .D(WriteData));
  SingleRegister singleregister_5 (.CLK(CLK), .WE(WE_4), .Q(singleregister_5_q), .reset(Reset), .D(WriteData));
  SingleRegister singleregister_6 (.CLK(CLK), .WE(WE_5), .Q(singleregister_6_q), .reset(Reset), .D(WriteData));
  SingleRegister singleregister_7 (.CLK(CLK), .WE(WE_6), .Q(singleregister_7_q), .reset(Reset), .D(WriteData));
  SingleRegister singleregister_8 (.CLK(CLK), .WE(WE_7), .Q(singleregister_8_q), .reset(Reset), .D(WriteData));
  Decoder #(.select(3), .enable("false")) decoder_1 (
    .out0(rs1_0), .out1(rs1_1), .out2(rs1_2), .out3(rs1_3), .out4(rs1_4), .out5(rs1_5), .out6(rs1_6),
    .out7(rs1_7), .sel(ReadReg1));
  Decoder #(.select(3), .enable("false")) decoder_2 (
    .out0(rs2_0), .out1(rs2_1), .out2(rs2_2), .out3(rs2_3), .out4(rs2_4), .out5(rs2_5), .out6(rs2_6),
    .out7(rs2_7), .sel(ReadReg2));
  Decoder #(.select(3), .enable("false")) decoder_3 (
    .out0(rd_0), .out1(rd_1), .out2(rd_2), .out3(rd_3), .out4(rd_4), .out5(rd_5), .out6(rd_6), .out7(rd_7),
    .sel(WriteReg));
  // Probe on singleregister_1_q
  // Probe on singleregister_2_q
  // Probe on singleregister_3_q
  // Probe on singleregister_4_q
  // Probe on singleregister_5_q
  // Probe on singleregister_6_q
  // Probe on singleregister_7_q
  // Probe on singleregister_8_q
  assign ReadData1 = rs1_0 ? singleregister_1_q : 16'bz;  // Controlled_Buffer controlled_buffer_1
  assign ReadData2 = rs2_0 ? singleregister_1_q : 16'bz;  // Controlled_Buffer controlled_buffer_2
  assign ReadData1 = rs1_1 ? singleregister_2_q : 16'bz;  // Controlled_Buffer controlled_buffer_3
  assign ReadData2 = rs2_1 ? singleregister_2_q : 16'bz;  // Controlled_Buffer controlled_buffer_4
  assign ReadData1 = rs1_2 ? singleregister_3_q : 16'bz;  // Controlled_Buffer controlled_buffer_5
  assign ReadData2 = rs2_2 ? singleregister_3_q : 16'bz;  // Controlled_Buffer controlled_buffer_6
  assign ReadData1 = rs1_3 ? singleregister_4_q : 16'bz;  // Controlled_Buffer controlled_buffer_7
  assign ReadData2 = rs2_3 ? singleregister_4_q : 16'bz;  // Controlled_Buffer controlled_buffer_8
  assign ReadData1 = rs1_4 ? singleregister_5_q : 16'bz;  // Controlled_Buffer controlled_buffer_9
  assign ReadData2 = rs2_4 ? singleregister_5_q : 16'bz;  // Controlled_Buffer controlled_buffer_10
  assign ReadData1 = rs1_5 ? singleregister_6_q : 16'bz;  // Controlled_Buffer controlled_buffer_11
  assign ReadData2 = rs2_5 ? singleregister_6_q : 16'bz;  // Controlled_Buffer controlled_buffer_12
  assign ReadData1 = rs1_6 ? singleregister_7_q : 16'bz;  // Controlled_Buffer controlled_buffer_13
  assign ReadData2 = rs2_6 ? singleregister_7_q : 16'bz;  // Controlled_Buffer controlled_buffer_14
  assign ReadData1 = rs1_7 ? singleregister_8_q : 16'bz;  // Controlled_Buffer controlled_buffer_15
  assign ReadData2 = rs2_7 ? singleregister_8_q : 16'bz;  // Controlled_Buffer controlled_buffer_16
  and and_1 (WE_0, rd_0, RegWriteEnable);
  and and_2 (WE_1, rd_1, RegWriteEnable);
  and and_3 (WE_2, rd_2, RegWriteEnable);
  and and_4 (WE_3, rd_3, RegWriteEnable);
  and and_5 (WE_4, rd_4, RegWriteEnable);
  and and_6 (WE_5, rd_5, RegWriteEnable);
  and and_7 (WE_6, rd_6, RegWriteEnable);
  and and_8 (WE_7, rd_7, RegWriteEnable);

  // Other names for the same wires on the sheet: RDVAL[15:0] = WriteData; WE = RegWriteEnable
endmodule

module memory_latch (
  input  [15:0] address,
  input  WE,
  input  clk,
  input  [15:0] data_in,
  output [15:0] address_latched,
  output WE_latched,
  output OE_latched,
  output [15:0] data_in_latched
);

  wire DMwe_latch_q;
  wire [15:0] addr_latch_q;

  Register #(.width(16), .trigger("falling")) addr_latch (
    .D(address), .en(WE), .clk(clk), .Q(addr_latch_q));  // open: clr
  D_Flip_Flop #(.trigger("falling")) DMwe_latch (.D(WE), .clk(clk), .Q(DMwe_latch_q));  // open: Qn, preset, reset
  Register #(.width(16), .trigger("falling")) data_to_be_written (
    .D(data_in), .en(WE), .clk(clk), .Q(data_in_latched));  // open: clr
  Multiplexer #(.width(16), .enable("false")) multiplexer_1 (
    .in0(address), .in1(addr_latch_q), .out(address_latched), .sel(DMwe_latch_q));
  and and_1 (WE_latched, clk, DMwe_latch_q);
  not not_1 (OE_latched, WE_latched);
endmodule

module ALU (
  input  [2:0] OpType,
  input  [15:0] InputData1,
  input  [15:0] InputData2,
  input  [2:0] Shamt,
  output [15:0] OutputData
);

  wire [15:0] and_1_out, multiplexer_1_out, multiplexer_2_out, multiplexer_3_out, multiplexer_4_out,
       multiplexer_5_out, multiplexer_6_out, ripplecarryadder_1_result, xor_1_out;

  Multiplexer #(.width(16), .enable("false")) multiplexer_1 (
    .in0(InputData1), .in1({InputData1[11:0], 4'b0000}), .out(multiplexer_1_out), .sel(Shamt[2]));
  Multiplexer #(.width(16), .enable("false")) multiplexer_2 (
    .in0(InputData1), .in1({4'b0000, InputData1[15:4]}), .out(multiplexer_2_out), .sel(Shamt[2]));
  assign and_1_out = InputData1 & InputData2;  // AND_Gate and_1, 16 bits wide
  assign xor_1_out = InputData1 ^ InputData2;  // XOR_Gate xor_1, 16 bits wide
  Multiplexer #(.width(16), .enable("false")) multiplexer_3 (
    .in0(multiplexer_1_out), .in1({multiplexer_1_out[13:0], 2'b00}), .out(multiplexer_3_out), .sel(Shamt[1]));
  Multiplexer #(.width(16), .enable("false")) multiplexer_4 (
    .in0(multiplexer_2_out), .in1({2'b00, multiplexer_2_out[15:2]}), .out(multiplexer_4_out), .sel(Shamt[1]));
  RippleCarryAdder ripplecarryadder_1 (
    .A(InputData1), .sub(OpType[0]), .B(InputData2), .result(ripplecarryadder_1_result));  // open: ovf
  Multiplexer #(.width(16), .enable("false")) multiplexer_5 (
    .in0(multiplexer_3_out), .in1({multiplexer_3_out[14:0], 1'b0}), .out(multiplexer_5_out), .sel(Shamt[0]));
  Multiplexer #(.width(16), .enable("false")) multiplexer_6 (
    .in0(multiplexer_4_out), .in1({1'b0, multiplexer_4_out[15:1]}), .out(multiplexer_6_out), .sel(Shamt[0]));
  Multiplexer #(.select(3), .width(16), .enable("false")) multiplexer_7 (
    .in0(ripplecarryadder_1_result), .in1(ripplecarryadder_1_result), .in2(and_1_out), .in3(xor_1_out),
    .in4(multiplexer_5_out), .in5(multiplexer_6_out), .out(OutputData), .sel(OpType));  // open: in6, in7

  // Other names for the same wires on the sheet: sub = OpType[0]; sh1 = Shamt[0]; sh2 = Shamt[1]; sh4 = Shamt[2]
endmodule

module RippleCarryAdder (
  input  [15:0] A,
  input  sub,
  input  [15:0] B,
  output [15:0] result,
  output ovf
);

  wire full_adder_1_cout, full_adder_2_cout, full_adder_3_cout, full_adder_4_cout, full_adder_5_cout,
       full_adder_6_cout, full_adder_7_cout, full_adder_8_cout, full_adder_9_cout, full_adder_10_cout,
       full_adder_11_cout, full_adder_12_cout, full_adder_13_cout, full_adder_14_cout, full_adder_15_cout,
       full_adder_16_cout, xor_1_out, xor_2_out, xor_3_out, xor_4_out, xor_5_out, xor_6_out, xor_7_out,
       xor_8_out, xor_9_out, xor_10_out, xor_11_out, xor_12_out, xor_13_out, xor_14_out, xor_15_out,
       xor_16_out;

  xor xor_1 (xor_1_out, B[0], sub);
  xor xor_2 (xor_2_out, B[1], sub);
  xor xor_3 (xor_3_out, B[2], sub);
  xor xor_4 (xor_4_out, B[3], sub);
  xor xor_5 (xor_5_out, B[4], sub);
  xor xor_6 (xor_6_out, B[5], sub);
  xor xor_7 (xor_7_out, B[6], sub);
  xor xor_8 (xor_8_out, B[7], sub);
  xor xor_9 (xor_9_out, B[8], sub);
  xor xor_10 (xor_10_out, B[9], sub);
  xor xor_11 (xor_11_out, B[10], sub);
  xor xor_12 (xor_12_out, B[11], sub);
  xor xor_13 (xor_13_out, B[12], sub);
  xor xor_14 (xor_14_out, B[13], sub);
  xor xor_15 (xor_15_out, B[14], sub);
  xor xor_16 (xor_16_out, B[15], sub);
  full_adder full_adder_1 (.Cout(full_adder_1_cout), .S(result[0]), .B(xor_1_out), .A(A[0]), .Cin(sub));
  full_adder full_adder_2 (.Cout(full_adder_2_cout), .S(result[1]), .B(xor_2_out), .A(A[1]), .Cin(full_adder_1_cout));
  full_adder full_adder_3 (.Cout(full_adder_3_cout), .S(result[2]), .B(xor_3_out), .A(A[2]), .Cin(full_adder_2_cout));
  full_adder full_adder_4 (.Cout(full_adder_4_cout), .S(result[3]), .B(xor_4_out), .A(A[3]), .Cin(full_adder_3_cout));
  full_adder full_adder_5 (.Cout(full_adder_5_cout), .S(result[4]), .B(xor_5_out), .A(A[4]), .Cin(full_adder_4_cout));
  full_adder full_adder_6 (.Cout(full_adder_6_cout), .S(result[5]), .B(xor_6_out), .A(A[5]), .Cin(full_adder_5_cout));
  full_adder full_adder_7 (.Cout(full_adder_7_cout), .S(result[6]), .B(xor_7_out), .A(A[6]), .Cin(full_adder_6_cout));
  full_adder full_adder_8 (.Cout(full_adder_8_cout), .S(result[7]), .B(xor_8_out), .A(A[7]), .Cin(full_adder_7_cout));
  full_adder full_adder_9 (.Cout(full_adder_9_cout), .S(result[8]), .B(xor_9_out), .A(A[8]), .Cin(full_adder_8_cout));
  full_adder full_adder_10 (
    .Cout(full_adder_10_cout), .S(result[9]), .B(xor_10_out), .A(A[9]), .Cin(full_adder_9_cout));
  full_adder full_adder_11 (
    .Cout(full_adder_11_cout), .S(result[10]), .B(xor_11_out), .A(A[10]), .Cin(full_adder_10_cout));
  full_adder full_adder_12 (
    .Cout(full_adder_12_cout), .S(result[11]), .B(xor_12_out), .A(A[11]), .Cin(full_adder_11_cout));
  full_adder full_adder_13 (
    .Cout(full_adder_13_cout), .S(result[12]), .B(xor_13_out), .A(A[12]), .Cin(full_adder_12_cout));
  full_adder full_adder_14 (
    .Cout(full_adder_14_cout), .S(result[13]), .B(xor_14_out), .A(A[13]), .Cin(full_adder_13_cout));
  full_adder full_adder_15 (
    .Cout(full_adder_15_cout), .S(result[14]), .B(xor_15_out), .A(A[14]), .Cin(full_adder_14_cout));
  full_adder full_adder_16 (
    .Cout(full_adder_16_cout), .S(result[15]), .B(xor_16_out), .A(A[15]), .Cin(full_adder_15_cout));
  xor xor_17 (ovf, full_adder_15_cout, full_adder_16_cout);
endmodule

module full_adder (
  input  Cin,
  input  A,
  input  B,
  output S,
  output Cout
);

  wire and_1_out, and_2_out, xor_1_out;

  and and_1 (and_1_out, B, A);
  xor xor_1 (xor_1_out, A, B);
  or or_1 (Cout, and_1_out, and_2_out);
  and and_2 (and_2_out, xor_1_out, Cin);
  xor xor_2 (S, Cin, xor_1_out);
endmodule

module InstructionDecoder (
  input  [15:0] Instruction,
  output [11:0] Address,
  output [5:0] Immediate,
  output [2:0] Rs,
  output [2:0] Rt,
  output [2:0] Rd,
  output [2:0] Shamt,
  output Rwe,
  output Rdst,
  output ALUinB,
  output ALUop2,
  output ALUop1,
  output ALUop0,
  output DMwe,
  output Rwd,
  output BR,
  output JP,
  output JR,
  output BEQ,
  output JAL,
  output inpu,
  output outpu
);

  wire [15:3] decoder_1_out3;

  Decoder #(.select(4), .enable("false")) decoder_1 (
    .out0(outpu), .out1(inpu), .out2(JAL), .out3(decoder_1_out3[3]), .out4(decoder_1_out3[4]),
    .out5(decoder_1_out3[5]), .out6(decoder_1_out3[6]), .out7(decoder_1_out3[7]), .out8(decoder_1_out3[8]),
    .out9(decoder_1_out3[9]), .out10(decoder_1_out3[10]), .out11(decoder_1_out3[11]),
    .out12(decoder_1_out3[12]), .out13(decoder_1_out3[13]), .out14(decoder_1_out3[14]),
    .out15(decoder_1_out3[15]), .sel(Instruction[15:12]));
  or or_1 (Rwe, JAL, decoder_1_out3[15], decoder_1_out3[14], decoder_1_out3[13], decoder_1_out3[12], decoder_1_out3[11], decoder_1_out3[10], decoder_1_out3[9], decoder_1_out3[8], inpu);
  or or_2 (Rdst, decoder_1_out3[15], decoder_1_out3[13], decoder_1_out3[12], decoder_1_out3[11], decoder_1_out3[10], decoder_1_out3[9]);
  or or_3 (ALUinB, decoder_1_out3[14], decoder_1_out3[8], decoder_1_out3[7]);
  or or_4 (ALUop2, decoder_1_out3[12], decoder_1_out3[11]);
  or or_5 (ALUop1, decoder_1_out3[10], decoder_1_out3[9]);
  or or_6 (ALUop0, decoder_1_out3[13], decoder_1_out3[11], decoder_1_out3[9], decoder_1_out3[6], decoder_1_out3[5]);
  or or_7 (DMwe, decoder_1_out3[7], decoder_1_out3[7]);
  or or_8 (Rwd, decoder_1_out3[8], decoder_1_out3[8]);
  or or_9 (BR, decoder_1_out3[6], decoder_1_out3[5]);
  or or_10 (JP, decoder_1_out3[4], JAL);
  buf or_11 (JR, decoder_1_out3[3]);  // OR_Gate
  buf or_12 (BEQ, decoder_1_out3[6]);  // OR_Gate

  assign Address = Instruction[11:0];
  assign Immediate = Instruction[5:0];
  assign Rd = Instruction[5:3];
  assign Rs = Instruction[11:9];
  assign Rt = Instruction[8:6];
  assign Shamt = Instruction[2:0];

  // Other names for the same wires on the sheet: Op[3:0] = Instruction[15:12]
endmodule
