// Logisim project my_adder.circ as structural Verilog: 2 circuits, main circuit RippleCarryAdder
module RippleCarryAdder (
  input  [15:0] A,
  input  sub,
  input  [15:0] B,
  output [15:0] result,
  output ovf
);

  wire full_adder_1_cout, full_adder_2_cout, full_adder_3_cout, full_adder_4_cout, full_adder_5_cout,
       full_adder_6_cout, full_adder_7_cout, full_adder_8_cout, full_adder_9_cout, full_adder_10_cout,
       full_adder_11_cout, full_adder_12_cout, full_adder_13_cout, full_adder_14_cout, full_adder_15_cout,
       full_adder_16_cout, xor_1_out, xor_2_out, xor_3_out, xor_4_out, xor_5_out, xor_6_out, xor_7_out,
       xor_8_out, xor_9_out, xor_10_out, xor_11_out, xor_12_out, xor_13_out, xor_14_out, xor_15_out,
       xor_16_out;

  xor xor_1 (xor_1_out, B[0], sub);
  xor xor_2 (xor_2_out, B[1], sub);
  xor xor_3 (xor_3_out, B[2], sub);
  xor xor_4 (xor_4_out, B[3], sub);
  xor xor_5 (xor_5_out, B[4], sub);
  xor xor_6 (xor_6_out, B[5], sub);
  xor xor_7 (xor_7_out, B[6], sub);
  xor xor_8 (xor_8_out, B[7], sub);
  xor xor_9 (xor_9_out, B[8], sub);
  xor xor_10 (xor_10_out, B[9], sub);
  xor xor_11 (xor_11_out, B[10], sub);
  xor xor_12 (xor_12_out, B[11], sub);
  xor xor_13 (xor_13_out, B[12], sub);
  xor xor_14 (xor_14_out, B[13], sub);
  xor xor_15 (xor_15_out, B[14], sub);
  xor xor_16 (xor_16_out, B[15], sub);
  full_adder full_adder_1 (.A(A[0]), .Cout(full_adder_1_cout), .B(xor_1_out), .S(result[0]), .Cin(sub));
  full_adder full_adder_2 (.A(A[1]), .Cout(full_adder_2_cout), .B(xor_2_out), .S(result[1]), .Cin(full_adder_1_cout));
  full_adder full_adder_3 (.A(A[2]), .Cout(full_adder_3_cout), .B(xor_3_out), .S(result[2]), .Cin(full_adder_2_cout));
  full_adder full_adder_4 (.A(A[3]), .Cout(full_adder_4_cout), .B(xor_4_out), .S(result[3]), .Cin(full_adder_3_cout));
  full_adder full_adder_5 (.A(A[4]), .Cout(full_adder_5_cout), .B(xor_5_out), .S(result[4]), .Cin(full_adder_4_cout));
  full_adder full_adder_6 (.A(A[5]), .Cout(full_adder_6_cout), .B(xor_6_out), .S(result[5]), .Cin(full_adder_5_cout));
  full_adder full_adder_7 (.A(A[6]), .Cout(full_adder_7_cout), .B(xor_7_out), .S(result[6]), .Cin(full_adder_6_cout));
  full_adder full_adder_8 (.A(A[7]), .Cout(full_adder_8_cout), .B(xor_8_out), .S(result[7]), .Cin(full_adder_7_cout));
  full_adder full_adder_9 (.A(A[8]), .Cout(full_adder_9_cout), .B(xor_9_out), .S(result[8]), .Cin(full_adder_8_cout));
  full_adder full_adder_10 (
    .A(A[9]), .Cout(full_adder_10_cout), .B(xor_10_out), .S(result[9]), .Cin(full_adder_9_cout));
  full_adder full_adder_11 (
    .A(A[10]), .Cout(full_adder_11_cout), .B(xor_11_out), .S(result[10]), .Cin(full_adder_10_cout));
  full_adder full_adder_12 (
    .A(A[11]), .Cout(full_adder_12_cout), .B(xor_12_out), .S(result[11]), .Cin(full_adder_11_cout));
  full_adder full_adder_13 (
    .A(A[12]), .Cout(full_adder_13_cout), .B(xor_13_out), .S(result[12]), .Cin(full_adder_12_cout));
  full_adder full_adder_14 (
    .A(A[13]), .Cout(full_adder_14_cout), .B(xor_14_out), .S(result[13]), .Cin(full_adder_13_cout));
  full_adder full_adder_15 (
    .A(A[14]), .Cout(full_adder_15_cout), .B(xor_15_out), .S(result[14]), .Cin(full_adder_14_cout));
  full_adder full_adder_16 (
    .A(A[15]), .Cout(full_adder_16_cout), .B(xor_16_out), .S(result[15]), .Cin(full_adder_15_cout));
  xor xor_17 (ovf, full_adder_15_cout, full_adder_16_cout);
endmodule

module full_adder (
  input  Cin,
  input  A,
  input  B,
  output S,
  output Cout
);

  wire and_1_out, and_2_out, xor_1_out;

  and and_1 (and_1_out, B, A);
  xor xor_1 (xor_1_out, A, B);
  or or_1 (Cout, and_1_out, and_2_out);
  and and_2 (and_2_out, xor_1_out, Cin);
  xor xor_2 (S, Cin, xor_1_out);
endmodule
